# Fritzing sketch capitulo1 (saved by Fritzing 0.9.3b)
breadboards: 1

parts:
  Part1 = Arduino Ethernet Shield (Rev3)
  LED1 = LED - 5mm [color="Red (633nm)" package="5 mm [THT]"]
  R1 = Resistor [tolerance=±5% resistance=220 package=THT]

nets:
  N1: Part1.5V, LED1.anode
  N2: Part1.GND, R1.Pin_0
  N3: LED1.cathode, R1.Pin_1
